# Fritzing sketch weather_dht22 (saved by Fritzing 0.8.7b)
breadboards: 1

parts:
  Part1 = Arduino Uno (Rev3)
  DHT22 = Humidity and Temperature Sensor RHT03
  R1 = Resistor [tolerance=±5% resistance=10k package=THT]

nets:
  N1: Part1.D2, DHT22.Data-signal, R1.Pin_1
  5V: Part1.5V, DHT22.Vcc, R1.Pin_0
  N2: Part1.GND, DHT22.GND_2
